# Fritzing sketch turbina (saved by Fritzing 0.9.6b)
breadboards: 1

parts:
  U1 = TLP621 [package=THT]
  U2 = TRIAC [package=to-92]
  R1 = Resistor [tolerance=±5% power=0.25 resistance=220 package=THT]
  C1 = Film/Foil Capacitor [capacitance=100nF voltage=35V package="22.5mm [THT, pp]"]
  D1 = Zener Diode [part_number=1N4732A breakdown_voltage=3.6V package="300 mil [THT]"]
  DS2Y-5-DC5V1 = DS2Y-5-DC5V [part_number=DS2Y-5-DC5V]
  V1 = AC Power [voltage=5 frequency=60]
  D2 = Rectifier Diode [package="Melf DO-213 AA [SMD]"]
  D3 = Rectifier Diode [package="Melf DO-213 AA [SMD]"]
  D4 = Rectifier Diode [package="Melf DO-213 AA [SMD]"]
  D5 = Rectifier Diode [package="Melf DO-213 AA [SMD]"]
  M1 = DC Motor
  C2 = Film/Foil Capacitor [capacitance=100nF voltage=35V package="22.5mm [THT, pp]"]
  D7 = Rectifier Diode [package="Melf DO-213 AA [SMD]"]
  D8 = Rectifier Diode [package="Melf DO-213 AA [SMD]"]
  C3 = Capacitor Polarized [package=nippon_f80]

nets:
  N1: U1.Pin_4, R1.Pin_0
  N2: U1.Pin_3, D1.anode, D8.anode, C3.-
  N3: U2.M1, D1.cathode, DS2Y-5-DC5V1.4_COM, V1.V+, D7.cathode, C3.+
  N4: U2.G, R1.Pin_1
  N5: U2.M2, C1.+
  N6: C1.-, D2.anode, D3.cathode
  N7: DS2Y-5-DC5V1.8_N.O., M1.pin_1
  N8: DS2Y-5-DC5V1.1_+, D2.cathode, D4.cathode
  N9: DS2Y-5-DC5V1.16_-, D3.anode, D5.anode
  N10: DS2Y-5-DC5V1.13_COM, V1.V-, D4.anode, D5.cathode, C2.+
  N11: DS2Y-5-DC5V1.9_N.O., M1.pin_2
  N12: C2.-, D7.anode, D8.cathode
